// Digital circuit cpu.dig as structural Verilog
module cpu (
  input  clk,
  input  in_2,
  input  in_3,
  input  in_4,
  input  in_5,
  input  in_14,
  input  in_15,
  input  in_18,
  input  in_19,
  input  in_20,
  input  in_21,
  input  in_22,
  input  in_23,
  input  in_24,
  input  in_25,
  input  in_26,
  input  in_27,
  input  in_28,
  input  in_29,
  input  in_30,
  input  in_31,
  input  in_32,
  input  in_33,
  input  in_34,
  input  in_51,
  input  in_52,
  input  in_53,
  input  in_54,
  input  in_55,
  input  in_56,
  input  in_57,
  input  in_58,
  input  in_66,
  input  in_67,
  input  in_68,
  input  in_69,
  input  in_70,
  input  in_71,
  input  in_72,
  input  in_73,
  input  in_84,
  input  in_85,
  output out_6,
  output Incrament,
  output Fetch,
  output Execute,
  output Decocde,
  output out_11,
  output out_12,
  output out_13,
  output out_16,
  output out_17,
  output out_35,
  output out_36,
  output out_37,
  output out_38,
  output out_39,
  output out_40,
  output out_41,
  output out_42,
  output out_43,
  output out_44,
  output out_45,
  output out_46,
  output out_47,
  output out_48,
  output out_49,
  output out_50,
  output out_59,
  output out_60,
  output out_61,
  output out_62,
  output out_63,
  output out_64,
  output out_65,
  output out_74,
  output out_75,
  output out_76,
  output out_77,
  output out_78,
  output out_79,
  output out_80,
  output out_81,
  output out_82,
  output out_83,
  output out_86,
  output out_87,
  output out_88,
  output out_89,
  output out_90,
  output out_91,
  output out_92,
  output out_93,
  output out_94,
  output out_95,
  output out_96,
  output out_97,
  output out_98,
  output out_99,
  output out_100,
  output out_101,
  output out_102,
  output out_103,
  output out_104,
  output out_105,
  output out_106,
  output out_107,
  output out_108,
  output out_109,
  output out_110,
  output out_111,
  output out_112,
  output out_113,
  output out_114,
  output out_115,
  output out_116,
  output out_117,
  output out_118,
  output out_119,
  output out_120,
  output out_121,
  output out_122,
  output out_123,
  output out_124,
  output out_125,
  output out_126,
  output out_127,
  output out_128,
  output out_129,
  output out_130
);

  wire add_1_c_o, add_1_s, add_2_c_o, add_2_s, add_3_c_o, add_3_s, add_4_c_o, add_4_s, add_5_c_o, add_5_s,
       add_6_c_o, add_6_s, add_7_c_o, add_7_s, add_8_s, and_1_out, and_2_out, and_3_out, and_4_out,
       and_5_out, and_6_out, and_7_out, and_8_out, and_9_out, and_10_out, and_11_out, and_12_out, and_13_out,
       and_14_out, and_15_out, and_16_out, and_17_out, and_18_out, and_19_out, and_20_out, and_21_out,
       and_22_out, and_23_out, and_24_out, and_25_out, and_26_out, and_27_out, and_28_out, and_29_out,
       and_30_out, and_31_out, and_32_out, and_33_out, and_34_out, and_35_out, and_36_out, and_37_out,
       and_38_out, and_39_out, and_40_out, and_41_out, and_42_out, and_43_out, and_44_out, and_45_out,
       and_46_out, and_47_out, and_48_out, and_49_out, and_51_out, and_52_out, and_53_out, and_54_out,
       and_55_out, and_56_out, and_57_out, and_58_out, and_59_out, and_60_out, and_61_out, and_62_out,
       and_63_out, and_64_out, and_65_out, and_66_out, and_67_out, and_68_out, and_69_out, and_70_out,
       and_71_out, and_72_out, and_73_out, and_74_out, and_75_out, and_76_out, and_77_out, and_78_out,
       and_79_out, and_80_out, and_81_out, and_82_out, and_83_out, and_84_out, and_85_out, and_86_out,
       and_87_out, and_88_out, and_89_out, and_90_out, and_91_out, d_ff_1_q, d_ff_as_31_q, d_ff_as_40_nq,
       multiplexer_1_out, multiplexer_2_out, multiplexer_3_out, multiplexer_4_out, multiplexer_5_out,
       multiplexer_6_out, multiplexer_7_out, multiplexer_8_out, multiplexer_9_out, multiplexer_10_out,
       multiplexer_11_out, multiplexer_12_out, multiplexer_13_out, multiplexer_14_out, multiplexer_15_out,
       multiplexer_16_out, multiplexer_17_out, multiplexer_18_out, multiplexer_19_out, multiplexer_20_out,
       multiplexer_21_out, multiplexer_22_out, multiplexer_23_out, multiplexer_24_out, multiplexer_25_out,
       multiplexer_27_out, multiplexer_28_out, multiplexer_29_out, multiplexer_30_out, multiplexer_31_out,
       multiplexer_32_out, multiplexer_33_out, multiplexer_34_out, multiplexer_36_out, multiplexer_37_out,
       multiplexer_38_out, multiplexer_39_out, multiplexer_40_out, nor_1_out, nor_2_out, nor_3_out,
       nor_4_out, not_1_out, not_2_out, not_3_out, not_4_out, not_5_out, not_6_out, not_7_out, not_8_out,
       not_9_out, not_10_out, not_11_out, not_12_out, not_13_out, not_14_out, not_15_out, not_16_out,
       not_17_out, not_18_out, not_19_out, not_20_out, not_21_out, not_22_out, not_23_out, not_24_out,
       not_25_out, not_26_out, not_27_out, not_28_out, not_29_out, not_30_out, not_31_out, not_32_out,
       not_33_out, not_34_out, not_35_out, not_36_out, not_37_out, not_38_out, not_39_out, not_40_out,
       not_41_out, not_42_out, not_43_out, not_44_out, not_45_out, or_1_out, or_2_out, or_3_out, or_4_out,
       or_5_out, or_6_out, or_7_out, or_8_out, or_9_out, or_10_out, or_11_out, xor_1_out, xor_2_out,
       xor_3_out, xor_4_out, xor_5_out, xor_6_out, xor_7_out;
  wire [1:0] ramdualport_1_d, ramdualport_1_d_2, ramdualport_1_d_3, ramdualport_1_d_4;
  wire [7:0] multiplexer_42_out;

  D_FF d_ff_1 (.D(in_84), .C(clk), .Q(d_ff_1_q), .nQ(out_83));
  and and_1 (and_1_out, or_11_out, clk);
  and and_2 (and_2_out, or_11_out, clk);
  and and_3 (and_3_out, or_11_out, clk);
  and and_4 (and_4_out, or_11_out, clk);
  and and_5 (and_5_out, or_11_out, clk);
  and and_6 (and_6_out, or_11_out, clk);
  and and_7 (and_7_out, or_11_out, clk);
  and and_8 (and_8_out, or_11_out, clk);
  not not_1 (not_1_out, out_35);
  D_FF_AS d_ff_as_1 (.Set(in_54), .D(multiplexer_33_out), .C(and_1_out), .Clr(d_ff_1_q), .Q(out_92), .nQ(out_65));
  D_FF_AS d_ff_as_2 (.Set(in_53), .D(multiplexer_34_out), .C(and_2_out), .Clr(d_ff_1_q), .Q(out_91), .nQ(out_64));
  D_FF_AS d_ff_as_3 (.Set(in_52), .D(or_6_out), .C(and_3_out), .Clr(d_ff_1_q), .Q(out_90), .nQ(out_87));
  D_FF_AS d_ff_as_4 (.Set(in_51), .D(multiplexer_36_out), .C(and_4_out), .Clr(d_ff_1_q), .Q(out_89), .nQ(out_63));
  D_FF_AS d_ff_as_5 (.Set(in_55), .D(multiplexer_37_out), .C(and_5_out), .Clr(d_ff_1_q), .Q(out_88), .nQ(out_62));
  D_FF_AS d_ff_as_6 (.Set(in_56), .D(multiplexer_38_out), .C(and_6_out), .Clr(d_ff_1_q), .Q(out_129), .nQ(out_61));
  D_FF_AS d_ff_as_7 (.Set(in_57), .D(multiplexer_39_out), .C(and_7_out), .Clr(d_ff_1_q), .Q(out_130), .nQ(out_60));
  D_FF_AS d_ff_as_8 (.Set(in_58), .D(multiplexer_40_out), .C(and_8_out), .Clr(d_ff_1_q), .Q(out_86), .nQ(out_59));
  not not_2 (not_2_out, not_1_out);
  and and_9 (and_9_out, Fetch, clk);
  and and_10 (and_10_out, Fetch, clk);
  and and_11 (and_11_out, Fetch, clk);
  and and_12 (and_12_out, Fetch, clk);
  and and_13 (and_13_out, Fetch, clk);
  and and_14 (and_14_out, Fetch, clk);
  and and_15 (and_15_out, Fetch, clk);
  and and_16 (and_16_out, Fetch, clk);
  and and_17 (and_17_out, Fetch, clk);
  and and_18 (and_18_out, Fetch, clk);
  and and_19 (and_19_out, Fetch, clk);
  and and_20 (and_20_out, Fetch, clk);
  and and_21 (and_21_out, Fetch, clk);
  and and_22 (and_22_out, Fetch, clk);
  and and_23 (and_23_out, Fetch, clk);
  and and_24 (and_24_out, Fetch, clk);
  or or_1 (or_1_out, and_40_out, and_48_out, and_48_out);
  D_FF_AS d_ff_as_9 (.Set(in_22), .D(ramdualport_1_d[0]), .C(and_9_out), .Clr(d_ff_1_q), .Q(out_116), .nQ(out_50));
  D_FF_AS d_ff_as_10 (.Set(in_21), .D(ramdualport_1_d[1]), .C(and_10_out), .Clr(d_ff_1_q), .Q(out_115), .nQ(out_49));
  D_FF_AS d_ff_as_11 (.Set(in_20), .D(ramdualport_1_d_2[0]), .C(and_11_out), .Clr(d_ff_1_q), .Q(out_114), .nQ(out_48));
  D_FF_AS d_ff_as_12 (.Set(in_19), .D(ramdualport_1_d_2[1]), .C(and_12_out), .Clr(d_ff_1_q), .Q(out_113), .nQ(out_47));
  D_FF_AS d_ff_as_13 (.Set(in_23), .D(ramdualport_1_d_3[0]), .C(and_13_out), .Clr(d_ff_1_q), .Q(out_112), .nQ(out_46));
  D_FF_AS d_ff_as_14 (.Set(in_24), .D(ramdualport_1_d_3[1]), .C(and_14_out), .Clr(d_ff_1_q), .Q(out_111), .nQ(out_45));
  D_FF_AS d_ff_as_15 (.Set(in_25), .D(ramdualport_1_d_4[0]), .C(and_15_out), .Clr(d_ff_1_q), .Q(out_110), .nQ(out_44));
  D_FF_AS d_ff_as_16 (.Set(in_26), .D(ramdualport_1_d_4[1]), .C(and_16_out), .Clr(d_ff_1_q), .Q(out_109), .nQ(out_43));
  D_FF_AS d_ff_as_17 (.Set(in_27), .D(out_93), .C(and_17_out), .Clr(d_ff_1_q), .Q(out_108), .nQ(out_42));
  D_FF_AS d_ff_as_18 (.Set(in_28), .D(out_94), .C(and_18_out), .Clr(d_ff_1_q), .Q(out_107), .nQ(out_41));
  D_FF_AS d_ff_as_19 (.Set(in_29), .D(out_95), .C(and_19_out), .Clr(d_ff_1_q), .Q(out_106), .nQ(out_40));
  D_FF_AS d_ff_as_20 (.Set(in_30), .D(out_96), .C(and_20_out), .Clr(d_ff_1_q), .Q(out_105), .nQ(out_39));
  D_FF_AS d_ff_as_21 (.Set(in_31), .D(out_97), .C(and_21_out), .Clr(d_ff_1_q), .Q(out_104), .nQ(out_38));
  D_FF_AS d_ff_as_22 (.Set(in_32), .D(out_98), .C(and_22_out), .Clr(d_ff_1_q), .Q(out_103), .nQ(out_37));
  D_FF_AS d_ff_as_23 (.Set(in_33), .D(out_99), .C(and_23_out), .Clr(d_ff_1_q), .Q(out_102), .nQ(out_36));
  D_FF_AS d_ff_as_24 (.Set(in_34), .D(out_100), .C(and_24_out), .Clr(d_ff_1_q), .Q(out_101), .nQ(out_35));
  and and_25 (and_25_out, 1'b1, d_ff_1_q);
  and and_26 (and_26_out, 1'b1, d_ff_1_q);
  and and_27 (and_27_out, or_1_out, clk);
  D_FF_AS d_ff_as_25 (.Set(in_15), .D(out_82), .C(and_26_out), .Clr(d_ff_1_q), .Q(out_117), .nQ(out_16));
  D_FF_AS d_ff_as_26 (.Set(in_14), .D(and_75_out), .C(and_27_out), .Clr(d_ff_1_q), .Q(out_118), .nQ(out_17));
  D_FF_AS d_ff_as_27 (.Set(d_ff_1_q), .D(Incrament), .C(and_25_out), .Clr(in_2), .Q(Fetch), .nQ(out_13));
  or or_2 (or_2_out, Decocde, Execute);
  and and_28 (and_28_out, out_42, not_3_out, out_40, not_4_out);
  not not_3 (not_3_out, out_41);
  not not_4 (not_4_out, out_39);
  and and_29 (and_29_out, out_42, out_41, out_40, not_5_out);
  not not_5 (not_5_out, out_39);
  and and_30 (and_30_out, not_6_out, not_7_out, not_8_out, not_9_out);
  not not_6 (not_6_out, out_42);
  not not_7 (not_7_out, out_41);
  not not_8 (not_8_out, out_40);
  not not_9 (not_9_out, out_39);
  and and_31 (and_31_out, not_10_out, out_41, not_11_out, not_12_out);
  not not_10 (not_10_out, out_42);
  not not_11 (not_11_out, out_40);
  not not_12 (not_12_out, out_39);
  and and_32 (and_32_out, out_42, not_13_out, not_14_out, not_15_out);
  not not_13 (not_13_out, out_41);
  not not_14 (not_14_out, out_40);
  not not_15 (not_15_out, out_39);
  and and_33 (and_33_out, out_42, not_16_out, not_17_out, out_39);
  not not_16 (not_16_out, out_41);
  not not_17 (not_17_out, out_40);
  and and_34 (and_34_out, not_18_out, out_41, out_40, not_19_out);
  not not_18 (not_18_out, out_42);
  not not_19 (not_19_out, out_39);
  and and_35 (and_35_out, not_20_out, not_21_out, not_22_out, out_39);
  not not_20 (not_20_out, out_42);
  not not_21 (not_21_out, out_41);
  not not_22 (not_22_out, out_40);
  D_FF_AS d_ff_as_28 (.Set(in_3), .D(Fetch), .C(and_25_out), .Clr(d_ff_1_q), .Q(Decocde), .nQ(out_12));
  D_FF_AS d_ff_as_29 (.Set(in_4), .D(Decocde), .C(and_25_out), .Clr(d_ff_1_q), .Q(Execute), .nQ(out_11));
  not not_23 (not_23_out, out_38);
  not not_24 (not_24_out, out_37);
  not not_25 (not_25_out, out_38);
  not not_26 (not_26_out, out_37);
  and and_36 (and_36_out, and_33_out, not_23_out, not_24_out);
  and and_37 (and_37_out, and_33_out, not_25_out, out_37);
  and and_38 (and_38_out, and_33_out, out_38, not_26_out);
  and and_39 (and_39_out, and_33_out, out_38, out_37);
  D_FF_AS d_ff_as_30 (.Set(in_5), .D(Execute), .C(and_25_out), .Clr(d_ff_1_q), .Q(Incrament), .nQ(out_6));
  and and_40 (and_40_out, and_31_out, or_2_out);
  and and_41 (and_41_out, and_30_out, or_2_out);
  and and_42 (and_42_out, and_29_out, or_2_out);
  and and_43 (and_43_out, and_28_out, or_2_out);
  and and_44 (and_44_out, and_36_out, or_2_out);
  and and_45 (and_45_out, and_32_out, or_2_out);
  and and_46 (and_46_out, and_37_out, or_2_out);
  and and_47 (and_47_out, and_38_out, or_2_out);
  and and_48 (and_48_out, and_39_out, or_2_out);
  and and_49 (and_49_out, and_34_out, or_2_out);
  and and_50 (and_48_out, and_35_out, or_2_out);
  and and_51 (and_51_out, and_44_out, out_17);
  and and_52 (and_52_out, and_46_out, out_17);
  and and_53 (and_53_out, and_47_out, out_16);
  and and_54 (and_54_out, and_48_out, out_16);
  or or_3 (or_3_out, and_45_out, and_44_out, and_46_out, Incrament, and_48_out);
  or or_4 (or_4_out, and_51_out, and_52_out, and_53_out, and_54_out, and_45_out);
  or or_5 (or_5_out, and_41_out, and_40_out, and_49_out, and_48_out, and_43_out);
  Multiplexer multiplexer_1 (.sel(Incrament), .in_0(out_81), .in_1(out_92), .out(multiplexer_1_out));
  Multiplexer multiplexer_2 (.sel(Incrament), .in_0(out_80), .in_1(out_91), .out(multiplexer_2_out));
  Multiplexer multiplexer_3 (.sel(Incrament), .in_0(out_79), .in_1(out_90), .out(multiplexer_3_out));
  Multiplexer multiplexer_4 (.sel(Incrament), .in_0(out_78), .in_1(out_89), .out(multiplexer_4_out));
  Multiplexer multiplexer_5 (.sel(Incrament), .in_0(out_77), .in_1(out_88), .out(multiplexer_5_out));
  Multiplexer multiplexer_6 (.sel(Incrament), .in_0(out_76), .in_1(out_129), .out(multiplexer_6_out));
  Multiplexer multiplexer_7 (.sel(Incrament), .in_0(out_75), .in_1(out_130), .out(multiplexer_7_out));
  Multiplexer multiplexer_8 (.sel(Incrament), .in_0(out_74), .in_1(out_86), .out(multiplexer_8_out));
  Multiplexer multiplexer_9 (.sel(or_9_out), .in_0(ramdualport_1_d[0]), .in_1(out_50), .out(multiplexer_9_out));
  Multiplexer multiplexer_10 (.sel(or_9_out), .in_0(ramdualport_1_d[1]), .in_1(out_49), .out(multiplexer_10_out));
  Multiplexer multiplexer_11 (.sel(or_9_out), .in_0(ramdualport_1_d_2[0]), .in_1(out_48), .out(multiplexer_11_out));
  Multiplexer multiplexer_12 (.sel(or_9_out), .in_0(ramdualport_1_d_2[1]), .in_1(out_47), .out(multiplexer_12_out));
  Multiplexer multiplexer_13 (.sel(or_9_out), .in_0(ramdualport_1_d_3[0]), .in_1(out_46), .out(multiplexer_13_out));
  Multiplexer multiplexer_14 (.sel(or_9_out), .in_0(ramdualport_1_d_3[1]), .in_1(out_45), .out(multiplexer_14_out));
  Multiplexer multiplexer_15 (.sel(or_9_out), .in_0(ramdualport_1_d_4[0]), .in_1(out_44), .out(multiplexer_15_out));
  Multiplexer multiplexer_16 (.sel(or_9_out), .in_0(ramdualport_1_d_4[1]), .in_1(out_43), .out(multiplexer_16_out));
  or or_6 (or_6_out, and_41_out, and_43_out, and_42_out, or_3_out);
  and and_55 (and_55_out, Execute, d_ff_as_31_q);
  and and_56 (and_56_out, Execute, or_4_out);
  not not_27 (not_27_out, or_4_out);
  and and_57 (and_57_out, Execute, and_42_out);
  or or_7 (or_7_out, and_48_out, and_43_out, and_41_out, or_3_out);
  or or_8 (or_8_out, Incrament, and_49_out);
  or or_9 (or_9_out, and_42_out, and_40_out, and_48_out, and_49_out);
  or or_10 (or_10_out, and_43_out, and_42_out);
  and and_58 (and_58_out, Execute, or_5_out);
  or or_11 (or_11_out, and_55_out, and_56_out);
  D_FF_AS d_ff_as_31 (.Set(in_18), .D(not_27_out), .C(clk), .Clr(d_ff_1_q), .Q(d_ff_as_31_q), .nQ(out_119));
  not not_28 (not_28_out, Incrament);
  not not_29 (not_29_out, not_28_out);
  not not_30 (not_30_out, not_29_out);
  not not_31 (not_31_out, not_28_out);
  not not_32 (not_32_out, not_31_out);
  not not_33 (not_33_out, not_28_out);
  not not_34 (not_34_out, not_33_out);
  not not_35 (not_35_out, not_28_out);
  not not_36 (not_36_out, not_35_out);
  not not_37 (not_37_out, not_28_out);
  not not_38 (not_38_out, not_37_out);
  not not_39 (not_39_out, not_28_out);
  not not_40 (not_40_out, not_39_out);
  not not_41 (not_41_out, not_28_out);
  not not_42 (not_42_out, not_41_out);
  not not_43 (not_43_out, not_28_out);
  not not_44 (not_44_out, not_43_out);
  and and_59 (and_59_out, multiplexer_1_out, multiplexer_9_out);
  and and_60 (and_60_out, multiplexer_2_out, multiplexer_10_out);
  and and_61 (and_61_out, multiplexer_3_out, multiplexer_11_out);
  and and_62 (and_62_out, multiplexer_4_out, multiplexer_12_out);
  and and_63 (and_63_out, multiplexer_5_out, multiplexer_13_out);
  and and_64 (and_64_out, multiplexer_6_out, multiplexer_14_out);
  and and_65 (and_65_out, multiplexer_7_out, multiplexer_15_out);
  and and_66 (and_66_out, multiplexer_8_out, multiplexer_16_out);
  xor xor_1 (xor_1_out, multiplexer_9_out, and_49_out);
  xor xor_2 (xor_2_out, multiplexer_10_out, and_49_out);
  xor xor_3 (xor_3_out, multiplexer_11_out, and_49_out);
  xor xor_4 (xor_4_out, multiplexer_12_out, and_49_out);
  xor xor_5 (xor_5_out, multiplexer_13_out, and_49_out);
  xor xor_6 (xor_6_out, multiplexer_14_out, and_49_out);
  xor xor_7 (xor_7_out, multiplexer_15_out, and_49_out);
  // XOr xor_8 has open pins: In_1=multiplexer_16_out, In_2=and_49_out, out=open
  and and_67 (and_67_out, not_30_out, xor_1_out);
  and and_68 (and_68_out, not_32_out, xor_2_out);
  and and_69 (and_69_out, not_34_out, xor_3_out);
  and and_70 (and_70_out, not_36_out, xor_4_out);
  and and_71 (and_71_out, not_38_out, xor_5_out);
  and and_72 (and_72_out, not_40_out, xor_6_out);
  and and_73 (and_73_out, not_42_out, xor_7_out);
  and and_74 (and_74_out, not_44_out, out_82);
  Add add_1 (.a(multiplexer_1_out), .b(and_67_out), .c_i(or_8_out), .s(add_1_s), .c_o(add_1_c_o));
  Add add_2 (.a(multiplexer_2_out), .b(and_68_out), .c_i(add_1_c_o), .s(add_2_s), .c_o(add_2_c_o));
  Add add_3 (.a(multiplexer_3_out), .b(and_69_out), .c_i(add_2_c_o), .s(add_3_s), .c_o(add_3_c_o));
  Add add_4 (.a(multiplexer_4_out), .b(and_70_out), .c_i(add_3_c_o), .s(add_4_s), .c_o(add_4_c_o));
  Add add_5 (.a(multiplexer_5_out), .b(and_71_out), .c_i(add_4_c_o), .s(add_5_s), .c_o(add_5_c_o));
  Add add_6 (.a(multiplexer_6_out), .b(and_72_out), .c_i(add_5_c_o), .s(add_6_s), .c_o(add_6_c_o));
  Add add_7 (.a(multiplexer_7_out), .b(and_73_out), .c_i(add_6_c_o), .s(add_7_s), .c_o(add_7_c_o));
  Add add_8 (.a(multiplexer_8_out), .b(and_74_out), .c_i(add_7_c_o), .s(add_8_s), .c_o(out_82));
  Multiplexer multiplexer_17 (
    .sel(or_7_out), .in_0(multiplexer_1_out), .in_1(multiplexer_9_out), .out(multiplexer_17_out));
  Multiplexer multiplexer_18 (
    .sel(or_7_out), .in_0(multiplexer_2_out), .in_1(multiplexer_10_out), .out(multiplexer_18_out));
  Multiplexer multiplexer_19 (
    .sel(or_7_out), .in_0(multiplexer_3_out), .in_1(multiplexer_11_out), .out(multiplexer_19_out));
  Multiplexer multiplexer_20 (
    .sel(or_7_out), .in_0(multiplexer_4_out), .in_1(multiplexer_12_out), .out(multiplexer_20_out));
  Multiplexer multiplexer_21 (
    .sel(or_7_out), .in_0(multiplexer_5_out), .in_1(multiplexer_13_out), .out(multiplexer_21_out));
  Multiplexer multiplexer_22 (
    .sel(or_7_out), .in_0(multiplexer_6_out), .in_1(multiplexer_14_out), .out(multiplexer_22_out));
  Multiplexer multiplexer_23 (
    .sel(or_7_out), .in_0(multiplexer_7_out), .in_1(multiplexer_15_out), .out(multiplexer_23_out));
  Multiplexer multiplexer_24 (
    .sel(or_7_out), .in_0(multiplexer_8_out), .in_1(multiplexer_16_out), .out(multiplexer_24_out));
  Multiplexer multiplexer_25 (.sel(or_7_out), .in_0(add_1_s), .in_1(and_59_out), .out(multiplexer_25_out));
  Multiplexer multiplexer_26 (.sel(or_7_out), .in_0(add_2_s), .in_1(and_60_out));  // open: out
  Multiplexer multiplexer_27 (.sel(or_7_out), .in_0(add_3_s), .in_1(and_61_out), .out(multiplexer_27_out));
  Multiplexer multiplexer_28 (.sel(or_7_out), .in_0(add_4_s), .in_1(and_62_out), .out(multiplexer_28_out));
  Multiplexer multiplexer_29 (.sel(or_7_out), .in_0(add_5_s), .in_1(and_63_out), .out(multiplexer_29_out));
  Multiplexer multiplexer_30 (.sel(or_7_out), .in_0(add_6_s), .in_1(and_64_out), .out(multiplexer_30_out));
  Multiplexer multiplexer_31 (.sel(or_7_out), .in_0(add_7_s), .in_1(and_65_out), .out(multiplexer_31_out));
  Multiplexer multiplexer_32 (.sel(or_7_out), .in_0(add_8_s), .in_1(and_66_out), .out(multiplexer_32_out));
  Multiplexer multiplexer_33 (
    .sel(or_6_out), .in_0(multiplexer_25_out), .in_1(multiplexer_17_out), .out(multiplexer_33_out));
  Multiplexer multiplexer_34 (.sel(or_6_out), .in_0(or_7_out), .in_1(multiplexer_18_out), .out(multiplexer_34_out));
  Multiplexer multiplexer_35 (.sel(or_6_out), .in_0(multiplexer_27_out), .in_1(multiplexer_19_out));  // open: out
  Multiplexer multiplexer_36 (
    .sel(or_6_out), .in_0(multiplexer_28_out), .in_1(multiplexer_20_out), .out(multiplexer_36_out));
  Multiplexer multiplexer_37 (
    .sel(or_6_out), .in_0(multiplexer_29_out), .in_1(multiplexer_21_out), .out(multiplexer_37_out));
  Multiplexer multiplexer_38 (
    .sel(or_6_out), .in_0(multiplexer_30_out), .in_1(multiplexer_22_out), .out(multiplexer_38_out));
  Multiplexer multiplexer_39 (
    .sel(or_6_out), .in_0(multiplexer_31_out), .in_1(multiplexer_23_out), .out(multiplexer_39_out));
  Multiplexer multiplexer_40 (
    .sel(or_6_out), .in_0(multiplexer_32_out), .in_1(multiplexer_24_out), .out(multiplexer_40_out));
  nor nor_1 (nor_1_out, multiplexer_33_out, multiplexer_34_out);
  nor nor_2 (nor_2_out, or_6_out, multiplexer_36_out);
  nor nor_3 (nor_3_out, multiplexer_37_out, multiplexer_38_out);
  nor nor_4 (nor_4_out, multiplexer_39_out, multiplexer_40_out);
  and and_75 (and_75_out, nor_1_out, nor_2_out, nor_3_out, nor_4_out);
  and and_76 (and_76_out, and_58_out, clk);
  and and_77 (and_77_out, and_58_out, clk);
  and and_78 (and_78_out, and_58_out, clk);
  and and_79 (and_79_out, and_58_out, clk);
  and and_80 (and_80_out, and_58_out, clk);
  and and_81 (and_81_out, and_58_out, clk);
  and and_82 (and_82_out, and_58_out, clk);
  and and_83 (and_83_out, and_58_out, clk);
  D_FF_AS d_ff_as_32 (.Set(in_69), .D(multiplexer_33_out), .C(and_76_out), .Clr(d_ff_1_q), .Q(out_127), .nQ(out_81));
  D_FF_AS d_ff_as_33 (.Set(in_68), .D(multiplexer_34_out), .C(and_77_out), .Clr(d_ff_1_q), .Q(out_126), .nQ(out_80));
  D_FF_AS d_ff_as_34 (.Set(in_67), .D(or_6_out), .C(and_78_out), .Clr(d_ff_1_q), .Q(out_125), .nQ(out_79));
  D_FF_AS d_ff_as_35 (.Set(in_66), .D(multiplexer_36_out), .C(and_79_out), .Clr(d_ff_1_q), .Q(out_124), .nQ(out_78));
  D_FF_AS d_ff_as_36 (.Set(in_70), .D(multiplexer_37_out), .C(and_80_out), .Clr(d_ff_1_q), .Q(out_123), .nQ(out_77));
  D_FF_AS d_ff_as_37 (.Set(in_71), .D(multiplexer_38_out), .C(and_81_out), .Clr(d_ff_1_q), .Q(out_122), .nQ(out_76));
  D_FF_AS d_ff_as_38 (.Set(in_72), .D(multiplexer_39_out), .C(and_82_out), .Clr(d_ff_1_q), .Q(out_121), .nQ(out_75));
  D_FF_AS d_ff_as_39 (.Set(in_73), .D(multiplexer_40_out), .C(and_83_out), .Clr(d_ff_1_q), .Q(out_120), .nQ(out_74));
  and and_84 (and_84_out, out_81, out_80);
  and and_85 (and_85_out, out_79, out_78);
  and and_86 (and_86_out, out_77, out_76);
  and and_87 (and_87_out, out_75, out_74);
  and and_88 (and_88_out, and_84_out, and_85_out);
  and and_89 (and_89_out, and_86_out, and_87_out);
  Multiplexer multiplexer_41 (.sel(or_10_out), .in_0(out_92), .in_1(out_50), .out(multiplexer_42_out[0]));
  Multiplexer multiplexer_42 (.sel(or_10_out), .in_0(out_91), .in_1(out_49), .out(multiplexer_42_out[1]));
  Multiplexer multiplexer_43 (.sel(or_10_out), .in_0(out_90), .in_1(out_48), .out(multiplexer_42_out[2]));
  Multiplexer multiplexer_44 (.sel(or_10_out), .in_0(out_89), .in_1(out_47), .out(multiplexer_42_out[3]));
  Multiplexer multiplexer_45 (.sel(or_10_out), .in_0(out_88), .in_1(out_46), .out(multiplexer_42_out[4]));
  Multiplexer multiplexer_46 (.sel(or_10_out), .in_0(out_129), .in_1(out_45), .out(multiplexer_42_out[5]));
  Multiplexer multiplexer_47 (.sel(or_10_out), .in_0(out_130), .in_1(out_44), .out(multiplexer_42_out[6]));
  Multiplexer multiplexer_48 (.sel(or_10_out), .in_0(out_86), .in_1(out_42), .out(multiplexer_42_out[7]));
  and and_90 (and_90_out, and_88_out, and_89_out);
  not not_45 (not_45_out, d_ff_1_q);
  and and_91 (and_91_out, and_90_out, and_76_out);
  D_FF_AS d_ff_as_40 (.Set(in_85), .D(not_2_out), .C(and_91_out), .Clr(d_ff_1_q), .Q(out_128), .nQ(d_ff_as_40_nq));
  RAMDualPort #(.AddrBits(8), .isProgramMemory("true"), .Bits(16)) ramdualport_1 (
    .A(multiplexer_42_out),
    .Din({out_35, {7{1'b0}}, out_74, out_75, out_76, out_77, out_78, out_79, out_80, out_81}),
    .str(and_57_out), .C(not_45_out), .ld(1'b1),
    .D({out_100, out_99, out_98, out_97, out_96, out_95, out_94, out_93, ramdualport_1_d_4, ramdualport_1_d_3, ramdualport_1_d_2, ramdualport_1_d}));
  // ScopeTrigger scopetrigger_1: pin names not known; wires that end beside it: d_ff_as_40_nq
endmodule
